# Fritzing sketch led_push_button (saved by Fritzing 0.7.10b)
breadboards: 1

parts:
  R1 = Resistor [tolerance=±5% resistance=10k package=THT]
  S1 = Pushbutton [package="[THT]"]
  LED1 = LED - 5mm [color="White (8000K)" package="5 mm [THT]"]
  Arduino1 = Arduino
  R2 = Resistor [tolerance=±5% resistance=10k package=THT]

nets:
  N1: R1.Pin_0, LED1.cathode, Arduino1.GND, R2.Pin_0, R2.Pin_1
  N2: R1.Pin_1, S1.Pin_3, S1.Pin_4, Arduino1.D7
  N3: S1.Pin_1, S1.Pin_2, Arduino1.+5V
  N4: LED1.anode, Arduino1.D9
